// Logisim project 18105226_陈宇卿.circ as structural Verilog: 12 circuits, main circuit main
module main (
  input  RESET
);

  wire ALUSrc, CLK, J_Sel, MemToReg, MemWr, nPC_sel, RegDst, RegWr, ZERO;
  wire [1:0] ALUctr, EXTOp;
  wire [4:0] multiplexer_1_out, rs, rt;
  wire [5:0] funct, opcode;
  wire [15:6] imm;
  wire [31:0] ALUOut, multiplexer_2_out, multiplexer_3_out, n18105226_dm_1_dataout,
       n18105226_ext_1_output_32, n18105226_gpr_1_busa, n18105226_gpr_1_busb;

  Clock #(.highDuration(1), .lowDuration(1)) u_CLK (.out(CLK));
  _18105226_IFU u_18105226_ifu_1 (
    .nPC_sel(nPC_sel), .ZERO(ZERO), .CLK(CLK), .RESET(RESET), .Instruction({opcode, rs, rt, imm, funct}),
    .J_Sel(J_Sel));
  Multiplexer #(.select(1), .width(5), .disabled("Z"), .enable("false")) multiplexer_1 (
    .in0(rt), .in1(imm[15:11]), .out(multiplexer_1_out), .sel(RegDst));
  _18105226_GPR u_18105226_gpr_1 (
    .WriteEnable(RegWr), .rw(multiplexer_1_out), .busW(multiplexer_3_out), .ra(rs), .rb(rt), .CLK(CLK),
    .RESET(RESET), .busB(n18105226_gpr_1_busb), .busA(n18105226_gpr_1_busa));
  _18105226_EXT u_18105226_ext_1 (.Input_16({imm, funct}), .ExtOp(EXTOp), .Output_32(n18105226_ext_1_output_32));
  Multiplexer #(.select(1), .width(32), .disabled("Z"), .enable("false")) multiplexer_2 (
    .in0(n18105226_gpr_1_busb), .in1(n18105226_ext_1_output_32), .out(multiplexer_2_out), .sel(ALUSrc));
  _18105226_CONTROL u_18105226_control_1 (
    .J_Sel(J_Sel), .opcode(opcode), .funct(funct), .RegDst(RegDst), .ALUSrc(ALUSrc), .MemToReg(MemToReg),
    .MemWr(MemWr), .RegWr(RegWr), .nPC_sel(nPC_sel), .EXTOp(EXTOp), .ALUctr(ALUctr));
  _18105226_ALU u_18105226_alu_1 (
    .ALUctr(ALUctr), .Source0(n18105226_gpr_1_busa), .Source1(multiplexer_2_out), .ZERO(ZERO), .ALUout(ALUOut));
  _18105226_DM u_18105226_dm_1 (
    .CLK(CLK), .Write_Enable(MemWr), .DataIn(n18105226_gpr_1_busb), .Address(ALUOut), .RESET(RESET),
    .DataOut(n18105226_dm_1_dataout));
  Multiplexer #(.select(1), .width(32), .disabled("Z"), .enable("false")) multiplexer_3 (
    .in0(ALUOut), .in1(n18105226_dm_1_dataout), .out(multiplexer_3_out), .sel(MemToReg));

  // Other names for the same wires on the sheet: imm[5:0] = funct; shamt[4:0] = imm[10:6]; rd[4:0] = imm[15:11]
endmodule

// IFU
module _18105226_IFU (
  input  nPC_sel,
  input  ZERO,
  input  J_Sel,
  input  CLK,
  input  RESET,
  output [31:0] Instruction
);

  wire BEQ_sel;
  wire [3:0] PC_4_31_28;
  wire [27:0] adder_2_out;
  wire [31:0] adder_1_out, bit_extender_1_out, multiplexer_1_out, PC_q, shifter_1_out;

  and and_1 (BEQ_sel, nPC_sel, ZERO);
  assign bit_extender_1_out = {{16{Instruction[15]}}, Instruction[15:0]};  // Bit_Extender bit_extender_1
  Shifter #(.width(32), .shift("ll")) shifter_1 (.in(bit_extender_1_out), .\dist (5'b00010), .out(shifter_1_out));
  Adder #(.width(32)) adder_1 (.a({PC_4_31_28, adder_2_out}), .b(shifter_1_out), .out(adder_1_out));  // open: cin, cout
  Adder #(.width(32)) adder_2 (.a(PC_q), .b(32'h4), .out({PC_4_31_28, adder_2_out}));  // open: cin, cout
  Multiplexer #(.select(2), .width(32), .disabled("Z"), .enable("false")) multiplexer_1 (
    .in0({PC_4_31_28, adder_2_out}), .in1(adder_1_out), .in2({PC_4_31_28, Instruction[25:0], 2'b00}),
    .out(multiplexer_1_out), .sel({J_Sel, BEQ_sel}));  // open: in3
  Register #(.width(32), .trigger("rising"), .Select("low")) PC (
    .D(multiplexer_1_out), .Q(PC_q), .clk(CLK), .clr(RESET));  // open: en
  ROM #(.addrWidth(8), .dataWidth(8), .Select("low")) ROM_0 (.addr(PC_q[9:2]), .data(Instruction[31:24]));
  ROM #(.addrWidth(8), .dataWidth(8), .Select("low")) ROM_1 (.addr(PC_q[9:2]), .data(Instruction[23:16]));
  ROM #(.addrWidth(8), .dataWidth(8), .Select("low")) ROM_2 (.addr(PC_q[9:2]), .data(Instruction[15:8]));
  ROM #(.addrWidth(8), .dataWidth(8), .Select("low")) ROM_3 (.addr(PC_q[9:2]), .data(Instruction[7:0]));
  // Probe on Instruction

  // Other names for the same wires on the sheet: imm16[15:0] = Instruction[15:0];
  //   target_address[25:0] = Instruction[25:0]

  // Notes on the sheet:
  //   00-PC+4 01-BEQ 10-J 
  //   contents of ROM_0 (hex, n*v repeats v):
  //   5*34 1 2 10 0 8 ac ac 0 10 8 2 2 8c 8c 3c 3c
  //   contents of ROM_1 (hex, n*v repeats v):
  //   21 42 63 84 a5 43 24 65 c3 0 3 4 83 64 0 2a 2a f 10 13 15
  //   contents of ROM_2 (hex, n*v repeats v):
  //   0 11 0 0 0 50 88 0 30 c 0 0 20 0 c 88 88 0 0 ff dc
  //   contents of ROM_3 (hex, n*v repeats v):
  //   10 1 a 64 a 21 21 2 21 c 4 c 23 1 c 23 23 4 c ab aa
endmodule

// 4bits ADD
module _18105226_4bit_ADDU (
  input  C0,
  input  A0,
  input  B0,
  input  A1,
  input  B1,
  input  A2,
  input  B2,
  input  A3,
  input  B3,
  output Sigma0,
  output Sigma1,
  output Sigma2,
  output Sigma3,
  output P0_star,
  output G0_star
);

  wire and_1_out, and_2_out, and_3_out, and_4_out, and_5_out, and_6_out, and_7_out, and_8_out, and_9_out,
       C1_out, C2_out, C3_out, G0, G1, G2, G3, P0, P1, P2, P3;

  and u_G0 (G0, A0, B0);
  xor u_P0 (P0, A0, B0);
  and u_G1 (G1, A1, B1);
  xor u_P1 (P1, A1, B1);
  and u_G2 (G2, A2, B2);
  xor u_P2 (P2, A2, B2);
  and u_G3 (G3, A3, B3);
  xor u_P3 (P3, A3, B3);
  xor u_Sigma0 (Sigma0, C0, P0);
  and and_1 (and_1_out, C0, P0);
  and and_2 (and_2_out, P1, G0);
  and and_3 (and_3_out, C0, P0, P1);
  and and_4 (and_4_out, G1, P2);
  and and_5 (and_5_out, P2, P1, G0);
  and and_6 (and_6_out, P2, P1, P0, C0);
  and and_7 (and_7_out, P3, G2);
  and and_8 (and_8_out, P3, P2, G1);
  and and_9 (and_9_out, P3, P2, P1, G0);
  or C1 (C1_out, and_1_out, G0);
  or C2 (C2_out, G1, and_2_out, and_3_out);
  or C3 (C3_out, G2, and_4_out, and_5_out, and_6_out);
  and and_10 (P0_star, P0, P1, P2, P3);
  or or_1 (G0_star, G3, and_7_out, and_8_out, and_9_out);
  xor u_Sigma1 (Sigma1, C1_out, P1);
  xor u_Sigma2 (Sigma2, C2_out, P2);
  xor u_Sigma3 (Sigma3, P3, C3_out);
endmodule

// 16bits Parallel Carry Link
module _18105226_Parallel_Carry_Link (
  input  C0,
  input  P0_star,
  input  G0_star,
  input  G1_star,
  input  P1_star,
  input  G2_star,
  input  P2_star,
  input  G3_star,
  input  P3_star,
  output C4,
  output C8,
  output C12,
  output C16
);

  wire and_1_out, and_2_out, and_3_out, and_4_out, and_5_out, and_6_out, and_7_out, and_8_out, and_9_out,
       nand_1_out, nor_1_out;

  and and_1 (and_1_out, C0, P0_star);
  and and_2 (and_2_out, C0, P0_star, P1_star);
  and and_3 (and_3_out, G0_star, P1_star);
  and and_4 (and_4_out, C0, P0_star, P1_star, P2_star);
  and and_5 (and_5_out, G0_star, P1_star, P2_star);
  and and_6 (and_6_out, G1_star, P2_star);
  and and_7 (and_7_out, G0_star, P1_star, P2_star, P3_star);
  and and_8 (and_8_out, G1_star, P2_star, P3_star);
  and and_9 (and_9_out, G2_star, P3_star);
  or or_1 (C4, and_1_out, G0_star);
  or or_2 (C8, and_2_out, and_3_out, G1_star);
  or or_3 (C12, and_4_out, and_5_out, and_6_out, G2_star);
  nor nor_1 (nor_1_out, and_7_out, and_8_out, and_9_out, G3_star);
  nand nand_1 (nand_1_out, C0, P0_star, P1_star, P2_star, P3_star);
  nand nand_2 (C16, nor_1_out, nand_1_out);
endmodule

// 16bits ADD
module _18105226_16bits_ADDU (
  input  [15:0] A_15_0,
  input  C0,
  input  [15:0] B_15_0,
  output C16,
  output [15:0] AddOut_15_0
);

  wire C4, C8, C12, n18105226_4bit_addu_1_g0_star, n18105226_4bit_addu_1_p0_star,
       n18105226_4bit_addu_2_g0_star, n18105226_4bit_addu_2_p0_star, n18105226_4bit_addu_3_g0_star,
       n18105226_4bit_addu_3_p0_star, n18105226_4bit_addu_4_g0_star, n18105226_4bit_addu_4_p0_star;

  _18105226_4bit_ADDU u_18105226_4bit_addu_1 (
    .C0(C0), .A0(A_15_0[0]), .B0(B_15_0[0]), .A1(A_15_0[1]), .B1(B_15_0[1]), .A2(A_15_0[2]), .B2(B_15_0[2]),
    .A3(A_15_0[3]), .B3(B_15_0[3]), .Sigma0(AddOut_15_0[0]), .Sigma1(AddOut_15_0[1]),
    .Sigma2(AddOut_15_0[2]), .Sigma3(AddOut_15_0[3]), .P0_star(n18105226_4bit_addu_1_p0_star),
    .G0_star(n18105226_4bit_addu_1_g0_star));
  _18105226_4bit_ADDU u_18105226_4bit_addu_2 (
    .C0(C4), .A0(A_15_0[4]), .B0(B_15_0[4]), .A1(A_15_0[5]), .B1(B_15_0[5]), .A2(A_15_0[6]), .B2(B_15_0[6]),
    .A3(A_15_0[7]), .B3(B_15_0[7]), .Sigma0(AddOut_15_0[4]), .Sigma1(AddOut_15_0[5]),
    .Sigma2(AddOut_15_0[6]), .Sigma3(AddOut_15_0[7]), .P0_star(n18105226_4bit_addu_2_p0_star),
    .G0_star(n18105226_4bit_addu_2_g0_star));
  _18105226_4bit_ADDU u_18105226_4bit_addu_3 (
    .C0(C8), .A0(A_15_0[8]), .B0(B_15_0[8]), .A1(A_15_0[9]), .B1(B_15_0[9]), .A2(A_15_0[10]),
    .B2(B_15_0[10]), .A3(A_15_0[11]), .B3(B_15_0[11]), .Sigma0(AddOut_15_0[8]), .Sigma1(AddOut_15_0[9]),
    .Sigma2(AddOut_15_0[10]), .Sigma3(AddOut_15_0[11]), .P0_star(n18105226_4bit_addu_3_p0_star),
    .G0_star(n18105226_4bit_addu_3_g0_star));
  _18105226_4bit_ADDU u_18105226_4bit_addu_4 (
    .C0(C12), .A0(A_15_0[12]), .B0(B_15_0[12]), .A1(A_15_0[13]), .B1(B_15_0[13]), .A2(A_15_0[14]),
    .B2(B_15_0[14]), .A3(A_15_0[15]), .B3(B_15_0[15]), .Sigma0(AddOut_15_0[12]), .Sigma1(AddOut_15_0[13]),
    .Sigma2(AddOut_15_0[14]), .Sigma3(AddOut_15_0[15]), .P0_star(n18105226_4bit_addu_4_p0_star),
    .G0_star(n18105226_4bit_addu_4_g0_star));
  _18105226_Parallel_Carry_Link u_18105226_parallel_carry_link_1 (
    .C0(C0), .P0_star(n18105226_4bit_addu_1_p0_star), .G0_star(n18105226_4bit_addu_1_g0_star),
    .G1_star(n18105226_4bit_addu_2_g0_star), .P1_star(n18105226_4bit_addu_2_p0_star),
    .G2_star(n18105226_4bit_addu_3_g0_star), .P2_star(n18105226_4bit_addu_3_p0_star),
    .G3_star(n18105226_4bit_addu_4_g0_star), .P3_star(n18105226_4bit_addu_4_p0_star), .C4(C4), .C8(C8),
    .C12(C12), .C16(C16));

  // Other names for the same wires on the sheet: A_3_0[3:0] = A_15_0[3:0]; A_7_4[3:0] = A_15_0[7:4];
  //   A_11_8[3:0] = A_15_0[11:8]; A_15_12[3:0] = A_15_0[15:12]; B_3_0[3:0] = B_15_0[3:0]; B_7_4[3:0] = B_15_0[7:4];
  //   B_11_8[3:0] = B_15_0[11:8]; B_15_12[3:0] = B_15_0[15:12]
endmodule

// 32bits ADDU
module _18105226_32bits_ADDU (
  input  [31:0] A_31_0,
  input  [31:0] B_31_0,
  output [31:0] AddOut_31_0
);

  wire n18105226_16bits_addu_1_c16;

  _18105226_16bits_ADDU u_18105226_16bits_addu_1 (
    .A_15_0(A_31_0[15:0]), .C0(1'b0), .B_15_0(B_31_0[15:0]), .C16(n18105226_16bits_addu_1_c16),
    .AddOut_15_0(AddOut_31_0[15:0]));
  _18105226_16bits_ADDU u_18105226_16bits_addu_2 (
    .A_15_0(A_31_0[31:16]), .C0(n18105226_16bits_addu_1_c16), .B_15_0(B_31_0[31:16]),
    .AddOut_15_0(AddOut_31_0[31:16]));  // open: C16
endmodule

// 32bits SUBU
module _18105226_32bits_SUBU (
  input  [31:0] A_31_0,
  input  [31:0] B_31_0,
  output [31:0] AddOut_31_0
);

  wire n18105226_16bits_addu_1_c16;
  wire [31:0] not_1_out;

  assign not_1_out = ~B_31_0;  // NOT_Gate not_1, 32 bits wide
  _18105226_16bits_ADDU u_18105226_16bits_addu_1 (
    .A_15_0(A_31_0[15:0]), .C0(1'b1), .B_15_0(not_1_out[15:0]), .C16(n18105226_16bits_addu_1_c16),
    .AddOut_15_0(AddOut_31_0[15:0]));
  _18105226_16bits_ADDU u_18105226_16bits_addu_2 (
    .A_15_0(A_31_0[31:16]), .C0(n18105226_16bits_addu_1_c16), .B_15_0(not_1_out[31:16]),
    .AddOut_15_0(AddOut_31_0[31:16]));  // open: C16
endmodule

// ALU
module _18105226_ALU (
  input  [1:0] ALUctr,
  input  [31:0] Source0,
  input  [31:0] Source1,
  output ZERO,
  output [31:0] ALUout
);

  wire [31:0] n18105226_32bits_addu_1_addout_31_0, n18105226_32bits_subu_1_addout_31_0, ORI_out;

  _18105226_32bits_ADDU u_18105226_32bits_addu_1 (
    .A_31_0(Source0), .B_31_0(Source1), .AddOut_31_0(n18105226_32bits_addu_1_addout_31_0));
  _18105226_32bits_SUBU u_18105226_32bits_subu_1 (
    .A_31_0(Source0), .B_31_0(Source1), .AddOut_31_0(n18105226_32bits_subu_1_addout_31_0));
  assign ORI_out = Source0 | Source1;  // OR_Gate ORI, 32 bits wide
  Multiplexer #(.select(2), .width(32), .disabled("Z"), .enable("false")) multiplexer_1 (
    .in0(n18105226_32bits_addu_1_addout_31_0), .in1(n18105226_32bits_subu_1_addout_31_0), .in2(ORI_out),
    .out(ALUout), .sel(ALUctr));  // open: in3
  nor nor_1 (ZERO, n18105226_32bits_subu_1_addout_31_0[0], n18105226_32bits_subu_1_addout_31_0[1], n18105226_32bits_subu_1_addout_31_0[2], n18105226_32bits_subu_1_addout_31_0[3], n18105226_32bits_subu_1_addout_31_0[4], n18105226_32bits_subu_1_addout_31_0[5], n18105226_32bits_subu_1_addout_31_0[6], n18105226_32bits_subu_1_addout_31_0[7], n18105226_32bits_subu_1_addout_31_0[8], n18105226_32bits_subu_1_addout_31_0[9], n18105226_32bits_subu_1_addout_31_0[10], n18105226_32bits_subu_1_addout_31_0[11], n18105226_32bits_subu_1_addout_31_0[12], n18105226_32bits_subu_1_addout_31_0[13], n18105226_32bits_subu_1_addout_31_0[14], n18105226_32bits_subu_1_addout_31_0[15], n18105226_32bits_subu_1_addout_31_0[17], n18105226_32bits_subu_1_addout_31_0[18], n18105226_32bits_subu_1_addout_31_0[19], n18105226_32bits_subu_1_addout_31_0[20], n18105226_32bits_subu_1_addout_31_0[21], n18105226_32bits_subu_1_addout_31_0[22], n18105226_32bits_subu_1_addout_31_0[23], n18105226_32bits_subu_1_addout_31_0[24], n18105226_32bits_subu_1_addout_31_0[25], n18105226_32bits_subu_1_addout_31_0[26], n18105226_32bits_subu_1_addout_31_0[27], n18105226_32bits_subu_1_addout_31_0[28], n18105226_32bits_subu_1_addout_31_0[29], n18105226_32bits_subu_1_addout_31_0[30], n18105226_32bits_subu_1_addout_31_0[31], n18105226_32bits_subu_1_addout_31_0[16]);

  // Notes on the sheet:
  //   00-ADDU 01-SUBU 10-ORI
endmodule

// GPR
module _18105226_GPR (
  input  WriteEnable,
  input  [4:0] rw,
  input  [31:0] busW,
  input  CLK,
  input  RESET,
  input  [4:0] ra,
  input  [4:0] rb,
  output [31:0] busA,
  output [31:0] busB
);

  wire demultiplexer_1_out1, demultiplexer_1_out2, demultiplexer_1_out3, demultiplexer_1_out4,
       demultiplexer_1_out5, demultiplexer_1_out6, demultiplexer_1_out7, demultiplexer_1_out8,
       demultiplexer_1_out9, demultiplexer_1_out10, demultiplexer_1_out11, demultiplexer_1_out12,
       demultiplexer_1_out13, demultiplexer_1_out14, demultiplexer_1_out15, demultiplexer_1_out16,
       demultiplexer_1_out17, demultiplexer_1_out18, demultiplexer_1_out19, demultiplexer_1_out20,
       demultiplexer_1_out21, demultiplexer_1_out22, demultiplexer_1_out23, demultiplexer_1_out24,
       demultiplexer_1_out25, demultiplexer_1_out26, demultiplexer_1_out27, demultiplexer_1_out28,
       demultiplexer_1_out29, demultiplexer_1_out30, demultiplexer_1_out31, undriven;
  wire [31:0] _0, _1, _2, _3, _4, _5, _6, _7, _8, _9, _10, _11, _12, _13, _14, _15, _16, _17, _18, _19, _20,
       _21, _22, _23, _24, _25, _26, _27, _28, _29, _30, _31;

  Multiplexer #(.select(5), .width(32), .disabled("Z"), .enable("false")) multiplexer_1 (
    .in0(_0), .in1(_1), .in2(_2), .in3(_3), .in4(_4), .in5(_5), .in6(_6), .in7(_7), .in8(_8), .in9(_9),
    .in10(_10), .in11(_11), .in12(_12), .in13(_13), .in14(_14), .in15(_15), .in16(_16), .in17(_17),
    .in18(_18), .in19(_19), .in20(_20), .in21(_21), .in22(_22), .in23(_23), .in24(_24), .in25(_25),
    .in26(_26), .in27(_27), .in28(_28), .in29(_29), .in30(_30), .in31(_31), .out(busA), .sel(ra));
  Multiplexer #(.select(5), .width(32), .disabled("Z"), .enable("false")) multiplexer_2 (
    .in0(_0), .in1(_1), .in2(_2), .in3(_3), .in4(_4), .in5(_5), .in6(_6), .in7(_7), .in8(_8), .in9(_9),
    .in10(_10), .in11(_11), .in12(_12), .in13(_13), .in14(_14), .in15(_15), .in16(_16), .in17(_17),
    .in18(_18), .in19(_19), .in20(_20), .in21(_21), .in22(_22), .in23(_23), .in24(_24), .in25(_25),
    .in26(_26), .in27(_27), .in28(_28), .in29(_29), .in30(_30), .in31(_31), .out(busB), .sel(rb));
  Demultiplexer #(.select(5), .width(1), .tristate("false"), .disabled("Z"), .enable("false")) demultiplexer_1 (
    .out1(demultiplexer_1_out1), .out2(demultiplexer_1_out2), .out3(demultiplexer_1_out3),
    .out4(demultiplexer_1_out4), .out5(demultiplexer_1_out5), .out6(demultiplexer_1_out6),
    .out7(demultiplexer_1_out7), .out8(demultiplexer_1_out8), .out9(demultiplexer_1_out9),
    .out10(demultiplexer_1_out10), .out11(demultiplexer_1_out11), .out12(demultiplexer_1_out12),
    .out13(demultiplexer_1_out13), .out14(demultiplexer_1_out14), .out15(demultiplexer_1_out15),
    .out16(demultiplexer_1_out16), .out17(demultiplexer_1_out17), .out18(demultiplexer_1_out18),
    .out19(demultiplexer_1_out19), .out20(demultiplexer_1_out20), .out21(demultiplexer_1_out21),
    .out22(demultiplexer_1_out22), .out23(demultiplexer_1_out23), .out24(demultiplexer_1_out24),
    .out25(demultiplexer_1_out25), .out26(demultiplexer_1_out26), .out27(demultiplexer_1_out27),
    .out28(demultiplexer_1_out28), .out29(demultiplexer_1_out29), .out30(demultiplexer_1_out30),
    .out31(demultiplexer_1_out31), .in(WriteEnable), .sel(rw));  // open: out0
  Register #(.width(32), .trigger("rising"), .Select("low")) register_1 (
    .Q(_0), .clk(CLK), .clr(RESET));  // open: D, en
  Register #(.width(32), .trigger("rising"), .Select("low")) register_2 (
    .D(busW), .en(demultiplexer_1_out1), .Q(_1), .clk(CLK), .clr(RESET));
  Register #(.width(32), .trigger("rising"), .Select("low")) register_3 (
    .D(busW), .en(demultiplexer_1_out2), .Q(_2), .clk(CLK), .clr(RESET));
  Register #(.width(32), .trigger("rising"), .Select("low")) register_4 (
    .D(busW), .en(demultiplexer_1_out3), .Q(_3), .clk(CLK), .clr(RESET));
  Register #(.width(32), .trigger("rising"), .Select("low")) register_5 (
    .D(busW), .en(demultiplexer_1_out4), .Q(_4), .clk(CLK), .clr(RESET));
  Register #(.width(32), .trigger("rising"), .Select("low")) register_6 (
    .D(busW), .en(demultiplexer_1_out5), .Q(_5), .clk(CLK), .clr(RESET));
  Register #(.width(32), .trigger("rising"), .Select("low")) register_7 (
    .D(busW), .en(demultiplexer_1_out6), .Q(_6), .clk(CLK), .clr(RESET));
  Register #(.width(32), .trigger("rising"), .Select("low")) register_8 (
    .D(busW), .en(demultiplexer_1_out7), .Q(_7), .clk(CLK), .clr(RESET));
  Register #(.width(32), .trigger("rising"), .Select("low")) register_9 (
    .D(busW), .en(demultiplexer_1_out8), .Q(_8), .clk(CLK), .clr(RESET), .cs(undriven));  // open: preset
  Register #(.width(32), .trigger("rising"), .Select("low")) register_10 (
    .D(busW), .en(demultiplexer_1_out9), .Q(_9), .clk(CLK), .clr(RESET));
  Register #(.width(32), .trigger("rising"), .Select("low")) register_11 (
    .D(busW), .en(demultiplexer_1_out10), .Q(_10), .clk(CLK), .clr(RESET));
  Register #(.width(32), .trigger("rising"), .Select("low")) register_12 (
    .D(busW), .en(demultiplexer_1_out11), .Q(_11), .clk(CLK), .clr(RESET));
  Register #(.width(32), .trigger("rising"), .Select("low")) register_13 (
    .D(busW), .en(demultiplexer_1_out12), .Q(_12), .clk(CLK), .clr(RESET));
  Register #(.width(32), .trigger("rising"), .Select("low")) register_14 (
    .D(busW), .en(demultiplexer_1_out13), .Q(_13), .clk(CLK), .clr(RESET));
  Register #(.width(32), .trigger("rising"), .Select("low")) register_15 (
    .D(busW), .en(demultiplexer_1_out14), .Q(_14), .clk(CLK), .clr(RESET));
  Register #(.width(32), .trigger("rising"), .Select("low")) register_16 (
    .D(busW), .en(demultiplexer_1_out15), .Q(_15), .clk(CLK), .clr(RESET));
  Register #(.width(32), .trigger("rising"), .Select("low")) register_17 (
    .D(busW), .en(demultiplexer_1_out16), .Q(_16), .clk(CLK), .clr(RESET));
  Register #(.width(32), .trigger("rising"), .Select("low")) register_18 (
    .D(busW), .en(demultiplexer_1_out17), .Q(_17), .clk(CLK), .clr(RESET));
  Register #(.width(32), .trigger("rising"), .Select("low")) register_19 (
    .D(busW), .en(demultiplexer_1_out18), .Q(_18), .clk(CLK), .clr(RESET));
  Register #(.width(32), .trigger("rising"), .Select("low")) register_20 (
    .D(busW), .en(demultiplexer_1_out19), .Q(_19), .clk(CLK), .clr(RESET));
  Register #(.width(32), .trigger("rising"), .Select("low")) register_21 (
    .D(busW), .en(demultiplexer_1_out20), .Q(_20), .clk(CLK), .clr(RESET));
  Register #(.width(32), .trigger("rising"), .Select("low")) register_22 (
    .D(busW), .en(demultiplexer_1_out21), .Q(_21), .clk(CLK), .clr(RESET));
  Register #(.width(32), .trigger("rising"), .Select("low")) register_23 (
    .D(busW), .en(demultiplexer_1_out22), .Q(_22), .clk(CLK), .clr(RESET));
  Register #(.width(32), .trigger("rising"), .Select("low")) register_24 (
    .D(busW), .en(demultiplexer_1_out23), .Q(_23), .clk(CLK), .clr(RESET));
  Register #(.width(32), .trigger("rising"), .Select("low")) register_25 (
    .D(busW), .en(demultiplexer_1_out24), .Q(_24), .clk(CLK), .clr(RESET));
  Register #(.width(32), .trigger("rising"), .Select("low")) register_26 (
    .D(busW), .en(demultiplexer_1_out25), .Q(_25), .clk(CLK), .clr(RESET));
  Register #(.width(32), .trigger("rising"), .Select("low")) register_27 (
    .D(busW), .en(demultiplexer_1_out26), .Q(_26), .clk(CLK), .clr(RESET));
  Register #(.width(32), .trigger("rising"), .Select("low")) register_28 (
    .D(busW), .en(demultiplexer_1_out27), .Q(_27), .clk(CLK), .clr(RESET));
  Register #(.width(32), .trigger("rising"), .Select("low")) register_29 (
    .D(busW), .en(demultiplexer_1_out28), .Q(_28), .clk(CLK), .clr(RESET));
  Register #(.width(32), .trigger("rising"), .Select("low")) register_30 (
    .D(busW), .en(demultiplexer_1_out29), .Q(_29), .clk(CLK), .clr(RESET));
  Register #(.width(32), .trigger("rising"), .Select("low")) register_31 (
    .D(busW), .en(demultiplexer_1_out30), .Q(_30), .clk(CLK), .clr(RESET));
  Register #(.width(32), .trigger("rising"), .Select("low")) register_32 (
    .D(busW), .en(demultiplexer_1_out31), .Q(_31), .clk(CLK), .clr(RESET));
endmodule

// DM
module _18105226_DM (
  input  CLK,
  input  Write_Enable,
  input  RESET,
  input  [31:0] DataIn,
  input  [31:0] Address,
  output [31:0] DataOut
);

  RAM #(.addrWidth(8), .dataWidth(8), .bus("separate"), .Select("low")) DM0 (
    .addr(Address[9:2]), .din(DataIn[7:0]), .data(DataOut[7:0]), .str(Write_Enable), .clk(CLK), .clr(RESET));  // open: sel, ld
  RAM #(.addrWidth(8), .dataWidth(8), .bus("separate"), .Select("low")) DM1 (
    .addr(Address[9:2]), .din(DataIn[15:8]), .data(DataOut[15:8]), .str(Write_Enable), .clk(CLK), .clr(RESET));  // open: sel, ld
  RAM #(.addrWidth(8), .dataWidth(8), .bus("separate"), .Select("low")) DM2 (
    .addr(Address[9:2]), .din(DataIn[23:16]), .data(DataOut[23:16]), .str(Write_Enable), .clk(CLK),
    .clr(RESET));  // open: sel, ld
  RAM #(.addrWidth(8), .dataWidth(8), .bus("separate"), .Select("low")) DM3 (
    .addr(Address[9:2]), .din(DataIn[31:24]), .data(DataOut[31:24]), .str(Write_Enable), .clk(CLK),
    .clr(RESET));  // open: sel, ld
endmodule

// EXT
module _18105226_EXT (
  input  [15:0] Input_16,
  input  [1:0] ExtOp,
  output [31:0] Output_32
);

  wire [31:0] bit_extender_1_out, bit_extender_2_out;

  assign bit_extender_1_out = {{16{1'b0}}, Input_16};  // Bit_Extender bit_extender_1
  assign bit_extender_2_out = {{16{Input_16[15]}}, Input_16};  // Bit_Extender bit_extender_2
  Multiplexer #(.select(2), .width(32), .disabled("Z"), .enable("false")) multiplexer_1 (
    .in0(bit_extender_1_out), .in1({Input_16, {16{1'b0}}}), .in2(bit_extender_2_out), .out(Output_32),
    .sel(ExtOp));  // open: in3

  // Notes on the sheet:
  //   00-高位零扩展 01-低位零扩展 10-符号扩展
endmodule

// CONTROL
module _18105226_CONTROL (
  input  [5:0] opcode,
  input  [5:0] funct,
  output RegDst,
  output ALUSrc,
  output MemToReg,
  output MemWr,
  output RegWr,
  output nPC_sel,
  output [1:0] EXTOp,
  output [1:0] ALUctr,
  output J_Sel
);

  wire ADDU_out, SUBU_out;

  and ADDU (ADDU_out, ~opcode[0], ~opcode[1], ~opcode[2], ~opcode[3], ~opcode[4], ~opcode[5], funct[0], ~funct[1], ~funct[2], ~funct[3], ~funct[4], funct[5]);  // AND_Gate
  and SUBU (SUBU_out, ~opcode[0], ~opcode[1], ~opcode[2], ~opcode[3], ~opcode[4], ~opcode[5], funct[0], funct[1], ~funct[2], ~funct[3], ~funct[4], funct[5]);  // AND_Gate
  and ORI (ALUctr[1], opcode[0], ~opcode[1], opcode[2], opcode[3], ~opcode[4], ~opcode[5]);  // AND_Gate
  and LW (MemToReg, opcode[0], opcode[1], ~opcode[2], ~opcode[3], ~opcode[4], opcode[5]);  // AND_Gate
  and SW (MemWr, opcode[0], opcode[1], ~opcode[2], opcode[3], ~opcode[4], opcode[5]);  // AND_Gate
  and BEQ (nPC_sel, ~opcode[0], ~opcode[1], opcode[2], ~opcode[3], ~opcode[4], ~opcode[5]);  // AND_Gate
  and LUI (EXTOp[0], opcode[0], opcode[1], opcode[2], opcode[3], ~opcode[4], ~opcode[5]);  // AND_Gate
  and J (J_Sel, ~opcode[0], opcode[1], ~opcode[2], ~opcode[3], ~opcode[4], ~opcode[5]);  // AND_Gate
  or or_1 (RegDst, ADDU_out, SUBU_out);
  or or_2 (ALUSrc, ALUctr[1], MemToReg, MemWr, EXTOp[0]);
  or or_3 (RegWr, ADDU_out, SUBU_out, ALUctr[1], MemToReg, EXTOp[0]);
  or or_4 (EXTOp[1], MemToReg, MemWr);
  or or_5 (ALUctr[0], nPC_sel, SUBU_out);
endmodule
