// Logisim project mips_lite.circ as structural Verilog: 11 circuits, main circuit main
// Control
module main (
  input  reset
);

  wire ALUSrc, CLK, lb, Mem2Reg, MemWr, pc_sel, RegDst, RegWr, zero;
  wire [1:0] ExtOp;
  wire [2:0] ALUCtr;
  wire [4:0] multiplexer_1_out;
  wire [5:0] ifu_1_insout_2, ifu_1_insout_3;
  wire [25:6] ifu_1_insout;
  wire [31:0] alu_1_result, dm_1_out, ext_1_b, gpr_1_busa, gpr_1_busb, multiplexer_2_out, multiplexer_3_out;

  // Probe on ifu_1_insout_2
  // Probe on ifu_1_insout_3
  // Probe on ifu_1_insout[15:11]
  // Probe on ifu_1_insout[20:16]
  // Probe on ifu_1_insout[25:21]
  // Probe on {ifu_1_insout_2, ifu_1_insout, ifu_1_insout_3}
  IFU ifu_1 (
    .pc_sel(pc_sel), .zero(zero), .insout({ifu_1_insout_2, ifu_1_insout, ifu_1_insout_3}), .clk(CLK),
    .reset(reset));
  Multiplexer #(.select(1), .width(5), .disabled("Z"), .enable("false")) multiplexer_1 (
    .in0(ifu_1_insout[20:16]), .in1(ifu_1_insout[15:11]), .out(multiplexer_1_out), .sel(RegDst));
  Control control_1 (
    .opcode(ifu_1_insout_2), .funct(ifu_1_insout_3), .RegDst(RegDst), .ALUSrc(ALUSrc), .MemtoReg(Mem2Reg),
    .RegWr(RegWr), .MemWr(MemWr), .nPC_sel(pc_sel), .ExtOp(ExtOp), .ALUCtr(ALUCtr), .lb(lb));
  GPR gpr_1 (
    .busW(multiplexer_3_out), .reset(reset), .regWr(RegWr), .rw(multiplexer_1_out), .ra(ifu_1_insout[25:21]),
    .rb(ifu_1_insout[20:16]), .clk(CLK), .busA(gpr_1_busa), .busB(gpr_1_busb));
  EXT ext_1 (.A({ifu_1_insout[15:6], ifu_1_insout_3}), .Extop(ExtOp), .B(ext_1_b));
  Clock #(.highDuration(1), .lowDuration(1)) clock_1 (.out(CLK));
  Multiplexer #(.select(1), .width(32), .disabled("Z"), .enable("false")) multiplexer_2 (
    .in0(gpr_1_busb), .in1(ext_1_b), .out(multiplexer_2_out), .sel(ALUSrc));
  Multiplexer #(.select(1), .width(32), .disabled("Z"), .enable("false")) multiplexer_3 (
    .in0(alu_1_result), .in1(dm_1_out), .out(multiplexer_3_out), .sel(Mem2Reg));
  // Probe on alu_1_result
  ALU alu_1 (.A(gpr_1_busa), .B(multiplexer_2_out), .ALUctr(ALUCtr), .Result(alu_1_result));
  nor nor_1 (zero, alu_1_result[0], alu_1_result[1], alu_1_result[2], alu_1_result[3], alu_1_result[4], alu_1_result[5], alu_1_result[6], alu_1_result[7], alu_1_result[8], alu_1_result[9], alu_1_result[10], alu_1_result[11], alu_1_result[12], alu_1_result[13], alu_1_result[14], alu_1_result[15], alu_1_result[17], alu_1_result[18], alu_1_result[19], alu_1_result[20], alu_1_result[21], alu_1_result[22], alu_1_result[23], alu_1_result[24], alu_1_result[25], alu_1_result[26], alu_1_result[27], alu_1_result[28], alu_1_result[29], alu_1_result[30], alu_1_result[31], alu_1_result[16]);
  DM dm_1 (
    .A(alu_1_result[6:2]), .D(gpr_1_busb), .out(dm_1_out), .Reset(reset), .MemWr(MemWr), .CLK(CLK), .lb(lb),
    .lbb(alu_1_result[1:0]));
endmodule

module IFU (
  input  clk,
  input  reset,
  input  pc_sel,
  input  zero,
  output [31:0] insout
);

  wire and_1_out, J_out;
  wire [29:0] beq_pc, bit_extender_1_out, multiplexer_1_out, multiplexer_2_out, pc_1, pc_q;

  Multiplexer #(.select(1), .width(30), .disabled("Z"), .enable("false")) multiplexer_1 (
    .in0(pc_1), .in1(beq_pc), .out(multiplexer_1_out), .sel(and_1_out));
  and and_1 (and_1_out, pc_sel, zero);
  Multiplexer #(.select(1), .width(30), .disabled("Z"), .enable("false")) multiplexer_2 (
    .in0(multiplexer_1_out), .in1({pc_1[29:26], insout[25:0]}), .out(multiplexer_2_out), .sel(J_out));
  Register #(.width(30), .trigger("rising"), .Select("low")) pc (
    .D(multiplexer_2_out), .Q(pc_q), .clk(clk), .clr(reset));  // open: en
  Adder_part #(.width(30)) adder_1 (.a(30'h1), .b(pc_q), .out(pc_1));  // open: cin, cout
  ROM #(.addrWidth(5), .dataWidth(32), .Select("high")) rom_1 (.addr(pc_q[4:0]), .data(insout));
  Adder_part #(.width(30)) adder_2 (.a(pc_1), .b(bit_extender_1_out), .out(beq_pc));  // open: cin, cout
  assign bit_extender_1_out = {{14{insout[15]}}, insout[15:0]};  // Bit_Extender bit_extender_1
  and J (J_out, ~insout[26], insout[27], ~insout[28], ~insout[29], ~insout[30], ~insout[31]);  // AND_Gate

  // Notes on the sheet:
  //   contents of rom_1 (hex, n*v repeats v):
  //   80490000 340600ae 664021 664823 12a0021 ac090010 8c0a0010 112a0002 3c0bcdcd 8000c0d 340befef
  //   3c094567 8000c07
endmodule

module GPR (
  input  clk,
  input  [31:0] busW,
  input  reset,
  input  regWr,
  input  [4:0] rw,
  input  [4:0] ra,
  input  [4:0] rb,
  output [31:0] busA,
  output [31:0] busB
);

  wire demultiplexer_1_out1, demultiplexer_1_out2, demultiplexer_1_out3, demultiplexer_1_out4,
       demultiplexer_1_out5, demultiplexer_1_out6, demultiplexer_1_out7, demultiplexer_1_out8,
       demultiplexer_1_out9, demultiplexer_1_out10, demultiplexer_1_out11, demultiplexer_1_out12,
       demultiplexer_1_out13, demultiplexer_1_out14, demultiplexer_1_out15, demultiplexer_1_out16,
       demultiplexer_1_out17, demultiplexer_1_out18, demultiplexer_1_out19, demultiplexer_1_out20,
       demultiplexer_1_out21, demultiplexer_1_out22, demultiplexer_1_out23, demultiplexer_1_out24,
       demultiplexer_1_out25, demultiplexer_1_out26, demultiplexer_1_out27, demultiplexer_1_out28,
       demultiplexer_1_out29, demultiplexer_1_out30, demultiplexer_1_out31;
  wire [31:0] _0, _1, _2, _3, _4, _5, _6, _7, _8, _9, _10, _11, _12, _13, _14, _15, _16, _17, _18, _19, _20,
       _21, _22, _23, _24, _25, _26, _27, _28, _29, _30, _31;

  Demultiplexer #(.select(5), .width(1), .tristate("false"), .disabled("Z"), .enable("false")) demultiplexer_1 (
    .out1(demultiplexer_1_out1), .out2(demultiplexer_1_out2), .out3(demultiplexer_1_out3),
    .out4(demultiplexer_1_out4), .out5(demultiplexer_1_out5), .out6(demultiplexer_1_out6),
    .out7(demultiplexer_1_out7), .out8(demultiplexer_1_out8), .out9(demultiplexer_1_out9),
    .out10(demultiplexer_1_out10), .out11(demultiplexer_1_out11), .out12(demultiplexer_1_out12),
    .out13(demultiplexer_1_out13), .out14(demultiplexer_1_out14), .out15(demultiplexer_1_out15),
    .out16(demultiplexer_1_out16), .out17(demultiplexer_1_out17), .out18(demultiplexer_1_out18),
    .out19(demultiplexer_1_out19), .out20(demultiplexer_1_out20), .out21(demultiplexer_1_out21),
    .out22(demultiplexer_1_out22), .out23(demultiplexer_1_out23), .out24(demultiplexer_1_out24),
    .out25(demultiplexer_1_out25), .out26(demultiplexer_1_out26), .out27(demultiplexer_1_out27),
    .out28(demultiplexer_1_out28), .out29(demultiplexer_1_out29), .out30(demultiplexer_1_out30),
    .out31(demultiplexer_1_out31), .in(regWr), .sel(rw));  // open: out0
  Multiplexer #(.select(5), .width(32), .disabled("Z"), .enable("false")) multiplexer_1 (
    .in0(_0), .in1(_1), .in2(_2), .in3(_3), .in4(_4), .in5(_5), .in6(_6), .in7(_7), .in8(_8), .in9(_9),
    .in10(_10), .in11(_11), .in12(_12), .in13(_13), .in14(_14), .in15(_15), .in16(_16), .in17(_17),
    .in18(_18), .in19(_19), .in20(_20), .in21(_21), .in22(_22), .in23(_23), .in24(_24), .in25(_25),
    .in26(_26), .in27(_27), .in28(_28), .in29(_29), .in30(_30), .in31(_31), .out(busA), .sel(ra));
  Multiplexer #(.select(5), .width(32), .disabled("Z"), .enable("false")) multiplexer_2 (
    .in0(_0), .in1(_1), .in2(_2), .in3(_3), .in4(_4), .in5(_5), .in6(_6), .in7(_7), .in8(_8), .in9(_9),
    .in10(_10), .in11(_11), .in12(_12), .in13(_13), .in14(_14), .in15(_15), .in16(_16), .in17(_17),
    .in18(_18), .in19(_19), .in20(_20), .in21(_21), .in22(_22), .in23(_23), .in24(_24), .in25(_25),
    .in26(_26), .in27(_27), .in28(_28), .in29(_29), .in30(_30), .in31(_31), .out(busB), .sel(rb));
  Register #(.width(32), .trigger("rising"), .Select("low")) u__0 (.Q(_0), .clr(reset));  // open: D, en, clk
  Register #(.width(32), .trigger("rising"), .Select("low")) u__1 (
    .D(busW), .en(demultiplexer_1_out1), .Q(_1), .clk(clk), .clr(reset));
  Register #(.width(32), .trigger("rising"), .Select("low")) u__2 (
    .D(busW), .en(demultiplexer_1_out2), .Q(_2), .clk(clk), .clr(reset));
  Register #(.width(32), .trigger("rising"), .Select("low")) u__3 (
    .D(busW), .en(demultiplexer_1_out3), .Q(_3), .clk(clk), .clr(reset));
  Register #(.width(32), .trigger("rising"), .Select("low")) u__4 (
    .D(busW), .en(demultiplexer_1_out4), .Q(_4), .clk(clk), .clr(reset));
  Register #(.width(32), .trigger("rising"), .Select("low")) u__5 (
    .D(busW), .en(demultiplexer_1_out5), .Q(_5), .clk(clk), .clr(reset));
  Register #(.width(32), .trigger("rising"), .Select("low")) u__6 (
    .D(busW), .en(demultiplexer_1_out6), .Q(_6), .clk(clk), .clr(reset));
  Register #(.width(32), .trigger("rising"), .Select("low")) u__7 (
    .D(busW), .en(demultiplexer_1_out7), .Q(_7), .clk(clk), .clr(reset));
  Register #(.width(32), .trigger("rising"), .Select("low")) u__8 (
    .D(busW), .en(demultiplexer_1_out8), .Q(_8), .clk(clk), .clr(reset));
  Register #(.width(32), .trigger("rising"), .Select("low")) u__9 (
    .D(busW), .en(demultiplexer_1_out9), .Q(_9), .clk(clk), .clr(reset));
  Register #(.width(32), .trigger("rising"), .Select("low")) u__10 (
    .D(busW), .en(demultiplexer_1_out10), .Q(_10), .clk(clk), .clr(reset));
  Register #(.width(32), .trigger("rising"), .Select("low")) u__11 (
    .D(busW), .en(demultiplexer_1_out11), .Q(_11), .clk(clk), .clr(reset));
  Register #(.width(32), .trigger("rising"), .Select("low")) u__12 (
    .D(busW), .en(demultiplexer_1_out12), .Q(_12), .clk(clk), .clr(reset));
  Register #(.width(32), .trigger("rising"), .Select("low")) u__13 (
    .D(busW), .en(demultiplexer_1_out13), .Q(_13), .clk(clk), .clr(reset));
  Register #(.width(32), .trigger("rising"), .Select("low")) u__14 (
    .D(busW), .en(demultiplexer_1_out14), .Q(_14), .clk(clk), .clr(reset));
  Register #(.width(32), .trigger("rising"), .Select("low")) u__15 (
    .D(busW), .en(demultiplexer_1_out15), .Q(_15), .clk(clk), .clr(reset));
  Register #(.width(32), .trigger("rising"), .Select("low")) u__16 (
    .D(busW), .en(demultiplexer_1_out16), .Q(_16), .clk(clk), .clr(reset));
  Register #(.width(32), .trigger("rising"), .Select("low")) u__17 (
    .D(busW), .en(demultiplexer_1_out17), .Q(_17), .clk(clk), .clr(reset));
  Register #(.width(32), .trigger("rising"), .Select("low")) u__18 (
    .D(busW), .en(demultiplexer_1_out18), .Q(_18), .clk(clk), .clr(reset));
  Register #(.width(32), .trigger("rising"), .Select("low")) u__19 (
    .D(busW), .en(demultiplexer_1_out19), .Q(_19), .clk(clk), .clr(reset));
  Register #(.width(32), .trigger("rising"), .Select("low")) u__20 (
    .D(busW), .en(demultiplexer_1_out20), .Q(_20), .clk(clk), .clr(reset));
  Register #(.width(32), .trigger("rising"), .Select("low")) u__21 (
    .D(busW), .en(demultiplexer_1_out21), .Q(_21), .clk(clk), .clr(reset));
  Register #(.width(32), .trigger("rising"), .Select("low")) u__22 (
    .D(busW), .en(demultiplexer_1_out22), .Q(_22), .clk(clk), .clr(reset));
  Register #(.width(32), .trigger("rising"), .Select("low")) u__23 (
    .D(busW), .en(demultiplexer_1_out23), .Q(_23), .clk(clk), .clr(reset));
  Register #(.width(32), .trigger("rising"), .Select("low")) u__24 (
    .D(busW), .en(demultiplexer_1_out24), .Q(_24), .clk(clk), .clr(reset));
  Register #(.width(32), .trigger("rising"), .Select("low")) u__25 (
    .D(busW), .en(demultiplexer_1_out25), .Q(_25), .clk(clk), .clr(reset));
  Register #(.width(32), .trigger("rising"), .Select("low")) u__26 (
    .D(busW), .en(demultiplexer_1_out26), .Q(_26), .clk(clk), .clr(reset));
  Register #(.width(32), .trigger("rising"), .Select("low")) u__27 (
    .D(busW), .en(demultiplexer_1_out27), .Q(_27), .clk(clk), .clr(reset));
  Register #(.width(32), .trigger("rising"), .Select("low")) u__28 (
    .D(busW), .en(demultiplexer_1_out28), .Q(_28), .clk(clk), .clr(reset));
  Register #(.width(32), .trigger("rising"), .Select("low")) u__29 (
    .D(busW), .en(demultiplexer_1_out29), .Q(_29), .clk(clk), .clr(reset));
  Register #(.width(32), .trigger("rising"), .Select("low")) u__30 (
    .D(busW), .en(demultiplexer_1_out30), .Q(_30), .clk(clk), .clr(reset));
  Register #(.width(32), .trigger("rising"), .Select("low")) u__31 (
    .D(busW), .en(demultiplexer_1_out31), .Q(_31), .clk(clk), .clr(reset));
endmodule

module ALU (
  input  [31:0] A,
  input  [31:0] B,
  input  [2:0] ALUctr,
  output [31:0] Result
);

  wire [31:0] n32adder_1_c, n32suber_1_c, ori_out;

  _32Adder u_32adder_1 (.A(A), .B(B), .C(n32adder_1_c));
  _32Suber u_32suber_1 (.A(A), .B(B), .C(n32suber_1_c));
  assign ori_out = A | B;  // OR_Gate ori, 32 bits wide
  Multiplexer #(.select(3), .width(32), .disabled("Z"), .enable("false")) multiplexer_1 (
    .in0(B), .in1(n32adder_1_c), .in2(n32suber_1_c), .in4(ori_out), .out(Result), .sel(ALUctr));  // open: in3, in5, in6, in7
endmodule

module Adder (
  input  A,
  input  B,
  input  CI,
  output S,
  output CO
);

  wire nand_1_out, nand_2_out, xor_1_out;

  xor xor_1 (xor_1_out, A, B);
  nand nand_1 (nand_1_out, B, A);
  xor xor_2 (S, xor_1_out, CI);
  nand nand_2 (nand_2_out, CI, xor_1_out);
  nand nand_3 (CO, nand_2_out, nand_1_out);
endmodule

module _32Adder (
  input  [31:0] A,
  input  [31:0] B,
  output [31:0] C
);

  wire adder_1_co, adder_2_co, adder_3_co, adder_4_co, adder_5_co, adder_6_co, adder_7_co, adder_8_co,
       adder_9_co, adder_10_co, adder_11_co, adder_12_co, adder_13_co, adder_14_co, adder_15_co, adder_16_co,
       adder_17_co, adder_18_co, adder_19_co, adder_20_co, adder_21_co, adder_22_co, adder_23_co,
       adder_24_co, adder_25_co, adder_26_co, adder_27_co, adder_28_co, adder_29_co, adder_30_co, adder_31_co;

  Adder adder_1 (.A(A[0]), .B(B[0]), .CI(1'b0), .S(C[0]), .CO(adder_1_co));
  Adder adder_2 (.A(A[1]), .B(B[1]), .CI(adder_1_co), .S(C[1]), .CO(adder_2_co));
  Adder adder_3 (.A(A[2]), .B(B[2]), .CI(adder_2_co), .S(C[2]), .CO(adder_3_co));
  Adder adder_4 (.A(A[3]), .B(B[3]), .CI(adder_3_co), .S(C[3]), .CO(adder_4_co));
  Adder adder_5 (.A(A[4]), .B(B[4]), .CI(adder_4_co), .S(C[4]), .CO(adder_5_co));
  Adder adder_6 (.A(A[5]), .B(B[5]), .CI(adder_5_co), .S(C[5]), .CO(adder_6_co));
  Adder adder_7 (.A(A[6]), .B(B[6]), .CI(adder_6_co), .S(C[6]), .CO(adder_7_co));
  Adder adder_8 (.A(A[7]), .B(B[7]), .CI(adder_7_co), .S(C[7]), .CO(adder_8_co));
  Adder adder_9 (.A(A[8]), .B(B[8]), .CI(adder_8_co), .S(C[8]), .CO(adder_9_co));
  Adder adder_10 (.A(A[9]), .B(B[9]), .CI(adder_9_co), .S(C[9]), .CO(adder_10_co));
  Adder adder_11 (.A(A[10]), .B(B[10]), .CI(adder_10_co), .S(C[10]), .CO(adder_11_co));
  Adder adder_12 (.A(A[11]), .B(B[11]), .CI(adder_11_co), .S(C[11]), .CO(adder_12_co));
  Adder adder_13 (.A(A[12]), .B(B[12]), .CI(adder_12_co), .S(C[12]), .CO(adder_13_co));
  Adder adder_14 (.A(A[13]), .B(B[13]), .CI(adder_13_co), .S(C[13]), .CO(adder_14_co));
  Adder adder_15 (.A(A[14]), .B(B[14]), .CI(adder_14_co), .S(C[14]), .CO(adder_15_co));
  Adder adder_16 (.A(A[15]), .B(B[15]), .CI(adder_15_co), .S(C[15]), .CO(adder_16_co));
  Adder adder_17 (.A(A[16]), .B(B[16]), .CI(adder_16_co), .S(C[16]), .CO(adder_17_co));
  Adder adder_18 (.A(A[17]), .B(B[17]), .CI(adder_17_co), .S(C[17]), .CO(adder_18_co));
  Adder adder_19 (.A(A[18]), .B(B[18]), .CI(adder_18_co), .S(C[18]), .CO(adder_19_co));
  Adder adder_20 (.A(A[19]), .B(B[19]), .CI(adder_19_co), .S(C[19]), .CO(adder_20_co));
  Adder adder_21 (.A(A[20]), .B(B[20]), .CI(adder_20_co), .S(C[20]), .CO(adder_21_co));
  Adder adder_22 (.A(A[21]), .B(B[21]), .CI(adder_21_co), .S(C[21]), .CO(adder_22_co));
  Adder adder_23 (.A(A[22]), .B(B[22]), .CI(adder_22_co), .S(C[22]), .CO(adder_23_co));
  Adder adder_24 (.A(A[23]), .B(B[23]), .CI(adder_23_co), .S(C[23]), .CO(adder_24_co));
  Adder adder_25 (.A(A[24]), .B(B[24]), .CI(adder_24_co), .S(C[24]), .CO(adder_25_co));
  Adder adder_26 (.A(A[25]), .B(B[25]), .CI(adder_25_co), .S(C[25]), .CO(adder_26_co));
  Adder adder_27 (.A(A[26]), .B(B[26]), .CI(adder_26_co), .S(C[26]), .CO(adder_27_co));
  Adder adder_28 (.A(A[27]), .B(B[27]), .CI(adder_27_co), .S(C[27]), .CO(adder_28_co));
  Adder adder_29 (.A(A[28]), .B(B[28]), .CI(adder_28_co), .S(C[28]), .CO(adder_29_co));
  Adder adder_30 (.A(A[29]), .B(B[29]), .CI(adder_29_co), .S(C[29]), .CO(adder_30_co));
  Adder adder_31 (.A(A[30]), .B(B[30]), .CI(adder_30_co), .S(C[30]), .CO(adder_31_co));
  Adder adder_32 (.A(A[31]), .B(B[31]), .CI(adder_31_co), .S(C[31]));  // open: CO

  // Other names for the same wires on the sheet: _0 = B[0]; _1 = B[1]; _2 = B[2]; _3 = B[3]; _4 = B[4]; _5 = B[5];
  //   _6 = B[6]; _7 = B[7]; _8 = B[8]; _9 = B[9]; _10 = B[10]; _11 = B[11]; _12 = B[12]; _13 = B[13]; _14 = B[14];
  //   _15 = B[15]; _16 = B[16]; _17 = B[17]; _18 = B[18]; _19 = B[19]; _20 = B[20]; _21 = B[21]; _22 = B[22];
  //   _23 = B[23]; _24 = B[24]; _25 = B[25]; _26 = B[26]; _27 = B[27]; _28 = B[28]; _29 = B[29]; _30 = B[30];
  //   _31 = B[31]
endmodule

module Suber (
  input  A,
  input  B,
  input  CI,
  output S,
  output CO
);

  wire nand_1_out, nand_2_out, not_1_out, xor_1_out;

  not not_1 (not_1_out, A);
  xor xor_1 (xor_1_out, B, CI);
  xor xor_2 (S, A, xor_1_out);
  nand nand_1 (nand_1_out, not_1_out, xor_1_out);
  nand nand_2 (nand_2_out, B, CI);
  nand nand_3 (CO, nand_1_out, nand_2_out);
endmodule

module _32Suber (
  input  [31:0] A,
  input  [31:0] B,
  output [31:0] C
);

  wire suber_1_co, suber_2_co, suber_3_co, suber_4_co, suber_5_co, suber_6_co, suber_7_co, suber_8_co,
       suber_9_co, suber_10_co, suber_11_co, suber_12_co, suber_13_co, suber_14_co, suber_15_co, suber_16_co,
       suber_17_co, suber_18_co, suber_19_co, suber_20_co, suber_21_co, suber_22_co, suber_23_co,
       suber_24_co, suber_25_co, suber_26_co, suber_27_co, suber_28_co, suber_29_co, suber_30_co, suber_31_co;

  Suber suber_1 (.A(A[0]), .B(B[0]), .CI(1'b0), .S(C[0]), .CO(suber_1_co));
  Suber suber_2 (.A(A[1]), .B(B[1]), .CI(suber_1_co), .S(C[1]), .CO(suber_2_co));
  Suber suber_3 (.A(A[2]), .B(B[2]), .CI(suber_2_co), .S(C[2]), .CO(suber_3_co));
  Suber suber_4 (.A(A[3]), .B(B[3]), .CI(suber_3_co), .S(C[3]), .CO(suber_4_co));
  Suber suber_5 (.A(A[4]), .B(B[4]), .CI(suber_4_co), .S(C[4]), .CO(suber_5_co));
  Suber suber_6 (.A(A[5]), .B(B[5]), .CI(suber_5_co), .S(C[5]), .CO(suber_6_co));
  Suber suber_7 (.A(A[6]), .B(B[6]), .CI(suber_6_co), .S(C[6]), .CO(suber_7_co));
  Suber suber_8 (.A(A[7]), .B(B[7]), .CI(suber_7_co), .S(C[7]), .CO(suber_8_co));
  Suber suber_9 (.A(A[8]), .B(B[8]), .CI(suber_8_co), .S(C[8]), .CO(suber_9_co));
  Suber suber_10 (.A(A[9]), .B(B[9]), .CI(suber_9_co), .S(C[9]), .CO(suber_10_co));
  Suber suber_11 (.A(A[10]), .B(B[10]), .CI(suber_10_co), .S(C[10]), .CO(suber_11_co));
  Suber suber_12 (.A(A[11]), .B(B[11]), .CI(suber_11_co), .S(C[11]), .CO(suber_12_co));
  Suber suber_13 (.A(A[12]), .B(B[12]), .CI(suber_12_co), .S(C[12]), .CO(suber_13_co));
  Suber suber_14 (.A(A[13]), .B(B[13]), .CI(suber_13_co), .S(C[13]), .CO(suber_14_co));
  Suber suber_15 (.A(A[14]), .B(B[14]), .CI(suber_14_co), .S(C[14]), .CO(suber_15_co));
  Suber suber_16 (.A(A[15]), .B(B[15]), .CI(suber_15_co), .S(C[15]), .CO(suber_16_co));
  Suber suber_17 (.A(A[16]), .B(B[16]), .CI(suber_16_co), .S(C[16]), .CO(suber_17_co));
  Suber suber_18 (.A(A[17]), .B(B[17]), .CI(suber_17_co), .S(C[17]), .CO(suber_18_co));
  Suber suber_19 (.A(A[18]), .B(B[18]), .CI(suber_18_co), .S(C[18]), .CO(suber_19_co));
  Suber suber_20 (.A(A[19]), .B(B[19]), .CI(suber_19_co), .S(C[19]), .CO(suber_20_co));
  Suber suber_21 (.A(A[20]), .B(B[20]), .CI(suber_20_co), .S(C[20]), .CO(suber_21_co));
  Suber suber_22 (.A(A[21]), .B(B[21]), .CI(suber_21_co), .S(C[21]), .CO(suber_22_co));
  Suber suber_23 (.A(A[22]), .B(B[22]), .CI(suber_22_co), .S(C[22]), .CO(suber_23_co));
  Suber suber_24 (.A(A[23]), .B(B[23]), .CI(suber_23_co), .S(C[23]), .CO(suber_24_co));
  Suber suber_25 (.A(A[24]), .B(B[24]), .CI(suber_24_co), .S(C[24]), .CO(suber_25_co));
  Suber suber_26 (.A(A[25]), .B(B[25]), .CI(suber_25_co), .S(C[25]), .CO(suber_26_co));
  Suber suber_27 (.A(A[26]), .B(B[26]), .CI(suber_26_co), .S(C[26]), .CO(suber_27_co));
  Suber suber_28 (.A(A[27]), .B(B[27]), .CI(suber_27_co), .S(C[27]), .CO(suber_28_co));
  Suber suber_29 (.A(A[28]), .B(B[28]), .CI(suber_28_co), .S(C[28]), .CO(suber_29_co));
  Suber suber_30 (.A(A[29]), .B(B[29]), .CI(suber_29_co), .S(C[29]), .CO(suber_30_co));
  Suber suber_31 (.A(A[30]), .B(B[30]), .CI(suber_30_co), .S(C[30]), .CO(suber_31_co));
  Suber suber_32 (.A(A[31]), .B(B[31]), .CI(suber_31_co), .S(C[31]));  // open: CO

  // Other names for the same wires on the sheet: _0 = B[0]; _1 = B[1]; _2 = B[2]; _3 = B[3]; _4 = B[4]; _5 = B[5];
  //   _6 = B[6]; _7 = B[7]; _8 = B[8]; _9 = B[9]; _10 = B[10]; _11 = B[11]; _12 = B[12]; _13 = B[13]; _14 = B[14];
  //   _15 = B[15]; _16 = B[16]; _17 = B[17]; _18 = B[18]; _19 = B[19]; _20 = B[20]; _21 = B[21]; _22 = B[22];
  //   _23 = B[23]; _24 = B[24]; _25 = B[25]; _26 = B[26]; _27 = B[27]; _28 = B[28]; _29 = B[29]; _30 = B[30];
  //   _31 = B[31]
endmodule

module EXT (
  input  [15:0] A,
  input  [1:0] Extop,
  output [31:0] B
);

  wire [31:0] bit_extender_1_out, bit_extender_2_out;

  assign bit_extender_1_out = {{16{1'b0}}, A};  // Bit_Extender bit_extender_1
  assign bit_extender_2_out = {{16{A[15]}}, A};  // Bit_Extender bit_extender_2
  Multiplexer #(.select(2), .width(32), .disabled("Z"), .enable("false")) multiplexer_1 (
    .in0(bit_extender_1_out), .in1({A, {16{1'b0}}}), .in2(bit_extender_2_out), .in3(bit_extender_2_out),
    .out(B), .sel(Extop));

  // Notes on the sheet:
  //   00：高位零扩展 01：低位零扩展 10：符号扩展
endmodule

module DM (
  input  lb,
  input  [1:0] lbb,
  input  [4:0] A,
  input  [31:0] D,
  input  MemWr,
  input  CLK,
  input  Reset,
  output [31:0] out
);

  wire [7:0] multiplexer_2_out;
  wire [31:0] bit_extender_1_out, ram_1_data;

  RAM #(.addrWidth(5), .dataWidth(32), .bus("separate"), .Select("high")) ram_1 (
    .addr(A), .din(D), .data(ram_1_data), .str(MemWr), .clk(CLK), .clr(Reset));  // open: sel, ld
  Multiplexer #(.select(1), .width(32), .disabled("Z"), .enable("false")) multiplexer_1 (
    .in0(ram_1_data), .in1(bit_extender_1_out), .out(out), .sel(lb));
  assign bit_extender_1_out = {{24{multiplexer_2_out[7]}}, multiplexer_2_out};  // Bit_Extender bit_extender_1
  Multiplexer #(.select(2), .width(8), .disabled("Z"), .enable("false")) multiplexer_2 (
    .in0(ram_1_data[7:0]), .in1(ram_1_data[15:8]), .in2(ram_1_data[23:16]), .in3(ram_1_data[31:24]),
    .out(multiplexer_2_out), .sel(lbb));
endmodule

module Control (
  input  [5:0] opcode,
  input  [5:0] funct,
  output RegDst,
  output ALUSrc,
  output MemtoReg,
  output RegWr,
  output MemWr,
  output nPC_sel,
  output [1:0] ExtOp,
  output [2:0] ALUCtr,
  output lb
);

  wire addu_out, lw_out, subu_out;

  and ori (ALUCtr[2], opcode[0], ~opcode[1], opcode[2], opcode[3], ~opcode[4], ~opcode[5]);  // AND_Gate
  and addu (addu_out, ~opcode[0], ~opcode[1], ~opcode[2], ~opcode[3], ~opcode[4], ~opcode[5], funct[0], ~funct[1], ~funct[2], ~funct[3], ~funct[4], funct[5]);  // AND_Gate
  and subu (subu_out, ~opcode[0], ~opcode[1], ~opcode[2], ~opcode[3], ~opcode[4], ~opcode[5], funct[0], funct[1], ~funct[2], ~funct[3], ~funct[4], funct[5]);  // AND_Gate
  and lw (lw_out, opcode[0], opcode[1], ~opcode[2], ~opcode[3], ~opcode[4], opcode[5]);  // AND_Gate
  and sw (MemWr, opcode[0], opcode[1], ~opcode[2], opcode[3], ~opcode[4], opcode[5]);  // AND_Gate
  and beq (nPC_sel, ~opcode[0], ~opcode[1], opcode[2], ~opcode[3], ~opcode[4], ~opcode[5]);  // AND_Gate
  and lui (ExtOp[0], opcode[0], opcode[1], opcode[2], opcode[3], ~opcode[4], ~opcode[5]);  // AND_Gate
  and u_lb (lb, ~opcode[0], ~opcode[1], ~opcode[2], ~opcode[3], ~opcode[4], opcode[5]);  // AND_Gate
  or or_1 (RegDst, addu_out, subu_out);
  or or_2 (ALUSrc, ALUCtr[2], lw_out, lb, ExtOp[0], MemWr);
  or or_3 (MemtoReg, lw_out, lb);
  or or_4 (RegWr, ExtOp[0], addu_out, subu_out, ALUCtr[2], lw_out, lb);
  or or_5 (ExtOp[1], lw_out, lb, MemWr);
  or or_6 (ALUCtr[1], subu_out, nPC_sel);
  or or_7 (ALUCtr[0], addu_out, lw_out, lb, MemWr);

  // Notes on the sheet:
  //   00：高位零扩展 01：低位零扩展 10：符号扩展
  //   000：保持busB 001：加法 010：减法 100：或
endmodule
